// Logisim project stack_logical_lite.circ as structural Verilog: 23 circuits, main circuit main
module main (
  input  CLK,
  input  RESET,
  input  [1:0] COMMAND,
  input  [2:0] INDEX,
  input  [3:0] IDATA,
  output [3:0] ODATA
);

  wire [3:0] stack_1_d0, stack_1_d1, stack_1_d2, stack_1_d3, stack_1_d4, stack_1_d5, stack_1_d6, stack_1_d7;

  stack stack_1 (
    .IDATA(IDATA), .CLK(CLK), .RESET(RESET), .COMMAND(COMMAND), .INDEX(INDEX), .ODATA(ODATA),
    .d0(stack_1_d0), .d1(stack_1_d1), .d2(stack_1_d2), .d3(stack_1_d3), .d4(stack_1_d4), .d5(stack_1_d5),
    .d6(stack_1_d6), .d7(stack_1_d7));
  // Probe on stack_1_d0
  // Probe on stack_1_d1
  // Probe on stack_1_d2
  // Probe on stack_1_d3
  // Probe on stack_1_d4
  // Probe on stack_1_d5
  // Probe on stack_1_d6
  // Probe on stack_1_d7
endmodule

module stack (
  input  [3:0] IDATA,
  input  CLK,
  input  RESET,
  input  [1:0] COMMAND,
  input  [2:0] INDEX,
  output [3:0] ODATA,
  output [3:0] d0,
  output [3:0] d1,
  output [3:0] d2,
  output [3:0] d3,
  output [3:0] d4,
  output [3:0] d5,
  output [3:0] d6,
  output [3:0] d7
);

  wire and_1_out, and_3_out, and_4_out, and_5_out, and_6_out, and_7_out, and_8_out, and_9_out, and_10_out,
       and_11_out, and_12_out, index_0_1_flag, index_0_2_flag, index_1_1_flag, index_1_2_flag,
       index_2_1_flag, index_2_2_flag, index_3_1_flag, index_3_2_flag, index_4_1_flag, index_4_2_flag,
       index_5_1_flag, index_5_2_flag, index_6_1_flag, index_6_2_flag, index_7_1_flag, index_7_2_flag,
       or_1_out, parse_command_1_get, parse_command_1_pop, parse_command_1_push;
  wire [2:0] adder_subtractor_1_res, adder_subtractor_2_res, and_2_out, conver_to_3_bit_1_out_bits,
       get_real_index_1_real_idx, incr_index_1_res_idx, incr_index_2_res_idx;
  wire [3:0] get_result_1_out_data, identification_1_out_3, identification_2_out_3, identification_3_out_3,
       identification_4_out_3, identification_5_out_3, identification_6_out_3, identification_7_out_3,
       identification_8_out_3;

  index_0 index_0_1 (.IDX(get_real_index_1_real_idx), .FLAG(index_0_1_flag));
  and and_1 (and_1_out, parse_command_1_push, CLK);
  incr_index incr_index_1 (.CLK(and_1_out), .RESET(RESET), .RES_IDX(incr_index_1_res_idx));
  adder_subtractor adder_subtractor_1 (
    .FIRST(incr_index_1_res_idx), .SECOND(incr_index_2_res_idx), .RES(adder_subtractor_1_res));  // open: out_4
  assign and_2_out = INDEX & conver_to_3_bit_1_out_bits;  // AND_Gate and_2, 3 bits wide
  adder_subtractor adder_subtractor_2 (
    .FIRST(adder_subtractor_1_res), .SECOND(and_2_out), .RES(adder_subtractor_2_res));  // open: out_4
  get_real_index get_real_index_1 (.FAKE_IDX(adder_subtractor_2_res), .REAL_IDX(get_real_index_1_real_idx));
  index_2 index_2_1 (.IDX(get_real_index_1_real_idx), .FLAG(index_2_1_flag));
  index_1 index_1_1 (.IDX(get_real_index_1_real_idx), .FLAG(index_1_1_flag));
  and and_3 (and_3_out, parse_command_1_pop, CLK);
  incr_index incr_index_2 (.CLK(and_3_out), .RESET(RESET), .RES_IDX(incr_index_2_res_idx));
  index_3 index_3_1 (.IDX(get_real_index_1_real_idx), .FLAG(index_3_1_flag));
  index_4 index_4_1 (.IDX(get_real_index_1_real_idx), .FLAG(index_4_1_flag));
  index_5 index_5_1 (.IDX(get_real_index_1_real_idx), .FLAG(index_5_1_flag));
  index_6 index_6_1 (.IDX(get_real_index_1_real_idx), .FLAG(index_6_1_flag));
  parse_command parse_command_1 (
    .in_1(COMMAND), .PUSH(parse_command_1_push), .POP(parse_command_1_pop), .GET(parse_command_1_get));  // open: FREE
  index_7 index_7_1 (.IDX(get_real_index_1_real_idx), .FLAG(index_7_1_flag));
  index_0 index_0_2 (.IDX(adder_subtractor_1_res), .FLAG(index_0_2_flag));
  index_1 index_1_2 (.IDX(adder_subtractor_1_res), .FLAG(index_1_2_flag));
  index_2 index_2_2 (.IDX(adder_subtractor_1_res), .FLAG(index_2_2_flag));
  index_3 index_3_2 (.IDX(adder_subtractor_1_res), .FLAG(index_3_2_flag));
  index_4 index_4_2 (.IDX(adder_subtractor_1_res), .FLAG(index_4_2_flag));
  index_5 index_5_2 (.IDX(adder_subtractor_1_res), .FLAG(index_5_2_flag));
  index_6 index_6_2 (.IDX(adder_subtractor_1_res), .FLAG(index_6_2_flag));
  index_7 index_7_2 (.IDX(adder_subtractor_1_res), .FLAG(index_7_2_flag));
  and and_4 (and_4_out, index_0_2_flag, parse_command_1_push);
  and and_5 (and_5_out, index_1_2_flag, parse_command_1_push);
  and and_6 (and_6_out, index_2_2_flag, parse_command_1_push);
  and and_7 (and_7_out, index_3_2_flag, parse_command_1_push);
  and and_8 (and_8_out, index_4_2_flag, parse_command_1_push);
  and and_9 (and_9_out, index_5_2_flag, parse_command_1_push);
  and and_10 (and_10_out, index_6_2_flag, parse_command_1_push);
  and and_11 (and_11_out, index_7_2_flag, parse_command_1_push);
  conver_to_3_bit conver_to_3_bit_1 (.IN_BITS(parse_command_1_get), .OUT_BITS(conver_to_3_bit_1_out_bits));
  or or_1 (or_1_out, parse_command_1_pop, parse_command_1_get);
  storage_bits storage_bits_1 (.CLK(CLK), .KEY(and_4_out), .RESET(RESET), .DATA(IDATA), .DATA_OUT(d0));
  storage_bits storage_bits_2 (.CLK(CLK), .KEY(and_5_out), .RESET(RESET), .DATA(IDATA), .DATA_OUT(d1));
  storage_bits storage_bits_3 (.CLK(CLK), .KEY(and_6_out), .RESET(RESET), .DATA(IDATA), .DATA_OUT(d2));
  storage_bits storage_bits_4 (.CLK(CLK), .KEY(and_7_out), .RESET(RESET), .DATA(IDATA), .DATA_OUT(d3));
  storage_bits storage_bits_5 (.CLK(CLK), .KEY(and_8_out), .RESET(RESET), .DATA(IDATA), .DATA_OUT(d4));
  storage_bits storage_bits_6 (.CLK(CLK), .KEY(and_9_out), .RESET(RESET), .DATA(IDATA), .DATA_OUT(d5));
  storage_bits storage_bits_7 (.CLK(CLK), .KEY(and_10_out), .RESET(RESET), .DATA(IDATA), .DATA_OUT(d6));
  storage_bits storage_bits_8 (.CLK(CLK), .KEY(and_11_out), .RESET(RESET), .DATA(IDATA), .DATA_OUT(d7));
  and and_12 (and_12_out, CLK, or_1_out);
  identification identification_1 (.CUR_DATA(d0), .GET_FLAG(index_0_1_flag), .out_3(identification_1_out_3));
  identification identification_2 (.CUR_DATA(d1), .GET_FLAG(index_1_1_flag), .out_3(identification_2_out_3));
  identification identification_3 (.CUR_DATA(d2), .GET_FLAG(index_2_1_flag), .out_3(identification_3_out_3));
  identification identification_4 (.CUR_DATA(d3), .GET_FLAG(index_3_1_flag), .out_3(identification_4_out_3));
  identification identification_5 (.CUR_DATA(d4), .GET_FLAG(index_4_1_flag), .out_3(identification_5_out_3));
  identification identification_6 (.CUR_DATA(d5), .GET_FLAG(index_5_1_flag), .out_3(identification_6_out_3));
  identification identification_7 (.CUR_DATA(d6), .GET_FLAG(index_6_1_flag), .out_3(identification_7_out_3));
  identification identification_8 (.CUR_DATA(d7), .GET_FLAG(index_7_1_flag), .out_3(identification_8_out_3));
  get_result get_result_1 (
    .ID0(identification_1_out_3), .ID1(identification_2_out_3), .ID2(identification_3_out_3),
    .ID3(identification_4_out_3), .ID4(identification_5_out_3), .ID5(identification_6_out_3),
    .ID6(identification_7_out_3), .ID7(identification_8_out_3), .OUT_DATA(get_result_1_out_data));
  storage_bits storage_bits_9 (
    .CLK(and_12_out), .KEY(and_12_out), .DATA(get_result_1_out_data), .DATA_OUT(ODATA));  // open: RESET

  // Notes on the sheet:
  //   your circuit must be here
endmodule

module rs (
  input  R,
  input  S,
  input  RESET,
  output Q,
  output NQ
);

  wire nor_2_out;

  nor nor_1 (Q, R, NQ);
  nor nor_2 (nor_2_out, Q, S);
  or or_1 (NQ, nor_2_out, RESET);
endmodule

module sync_rs (
  input  R,
  input  CLK,
  input  S,
  input  RESET,
  output Q,
  output NQ
);

  wire and_1_out, and_2_out, or_1_out, por_1_out;

  POR por_1 (.out(por_1_out));
  and and_1 (and_1_out, R, CLK);
  and and_2 (and_2_out, CLK, S);
  or or_1 (or_1_out, RESET, por_1_out);
  rs rs_1 (.R(and_1_out), .S(and_2_out), .RESET(or_1_out), .Q(Q), .NQ(NQ));
endmodule

module parse_command (
  input  [1:0] in_1,
  output PUSH,
  output POP,
  output GET,
  output FREE
);

  wire not_1_out, not_2_out;

  not not_1 (not_1_out, in_1[0]);
  not not_2 (not_2_out, in_1[1]);
  and and_1 (PUSH, in_1[0], not_2_out);
  and and_2 (GET, in_1[0], in_1[1]);
  and and_3 (POP, not_1_out, in_1[1]);
  and and_4 (FREE, not_1_out, not_2_out);
endmodule

module d_trigger (
  input  CLK,
  input  D,
  input  RESET,
  output Q,
  output NQ
);

  wire not_1_out;

  not not_1 (not_1_out, D);
  sync_rs sync_rs_1 (.R(not_1_out), .CLK(CLK), .S(D), .RESET(RESET), .Q(Q), .NQ(NQ));
endmodule

module storage_bits (
  input  CLK,
  input  KEY,
  input  RESET,
  input  [3:0] DATA,
  output [3:0] DATA_OUT
);

  wire and_1_out;

  and and_1 (and_1_out, CLK, KEY);
  d_trigger d_trigger_1 (.CLK(and_1_out), .D(DATA[0]), .RESET(RESET), .Q(DATA_OUT[0]));  // open: NQ
  d_trigger d_trigger_2 (.CLK(and_1_out), .D(DATA[1]), .RESET(RESET), .Q(DATA_OUT[1]));  // open: NQ
  d_trigger d_trigger_3 (.CLK(and_1_out), .D(DATA[2]), .RESET(RESET), .Q(DATA_OUT[2]));  // open: NQ
  d_trigger d_trigger_4 (.CLK(and_1_out), .D(DATA[3]), .RESET(RESET), .Q(DATA_OUT[3]));  // open: NQ
endmodule

module index_0 (
  input  [2:0] IDX,
  output FLAG
);

  wire not_1_out, not_2_out, not_3_out;

  not not_1 (not_1_out, IDX[0]);
  not not_2 (not_2_out, IDX[1]);
  not not_3 (not_3_out, IDX[2]);
  and and_1 (FLAG, not_1_out, not_2_out, not_3_out);
endmodule

module index_1 (
  input  [2:0] IDX,
  output FLAG
);

  wire not_1_out, not_2_out;

  not not_1 (not_1_out, IDX[1]);
  not not_2 (not_2_out, IDX[2]);
  and and_1 (FLAG, IDX[0], not_1_out, not_2_out);
endmodule

module index_2 (
  input  [2:0] IDX,
  output FLAG
);

  wire not_1_out, not_2_out;

  not not_1 (not_1_out, IDX[0]);
  not not_2 (not_2_out, IDX[2]);
  and and_1 (FLAG, not_1_out, IDX[1], not_2_out);
endmodule

module index_3 (
  input  [2:0] IDX,
  output FLAG
);

  wire not_1_out;

  not not_1 (not_1_out, IDX[2]);
  and and_1 (FLAG, IDX[0], IDX[1], not_1_out);
endmodule

module index_4 (
  input  [2:0] IDX,
  output FLAG
);

  wire not_1_out, not_2_out;

  not not_1 (not_1_out, IDX[0]);
  not not_2 (not_2_out, IDX[1]);
  and and_1 (FLAG, not_1_out, not_2_out, IDX[2]);
endmodule

module index_5 (
  input  [2:0] IDX,
  output FLAG
);

  wire not_1_out;

  not not_1 (not_1_out, IDX[1]);
  and and_1 (FLAG, IDX[0], not_1_out, IDX[2]);
endmodule

module index_6 (
  input  [2:0] IDX,
  output FLAG
);

  wire not_1_out;

  not not_1 (not_1_out, IDX[0]);
  and and_1 (FLAG, not_1_out, IDX[1], IDX[2]);
endmodule

module index_7 (
  input  [2:0] IDX,
  output FLAG
);

  and and_1 (FLAG, IDX[0], IDX[1], IDX[2]);
endmodule

module incr_index (
  input  CLK,
  input  RESET,
  output [2:0] RES_IDX
);

  wire and_1_out;

  jk_trigger jk_trigger_1 (.K(1'b1), .CLK(CLK), .J(1'b1), .RESET(RESET), .Q(RES_IDX[0]));  // open: NQ
  jk_trigger jk_trigger_2 (.K(RES_IDX[0]), .CLK(CLK), .J(RES_IDX[0]), .RESET(RESET), .Q(RES_IDX[1]));  // open: NQ
  jk_trigger jk_trigger_3 (.K(and_1_out), .CLK(CLK), .J(and_1_out), .RESET(RESET), .Q(RES_IDX[2]));  // open: NQ
  and and_1 (and_1_out, RES_IDX[0], RES_IDX[1]);
endmodule

module jk_trigger (
  input  K,
  input  CLK,
  input  J,
  input  RESET,
  output Q,
  output NQ
);

  wire and_1_out, and_2_out, not_1_out, sync_rs_1_nq, sync_rs_1_q;

  and and_1 (and_1_out, Q, K);
  and and_2 (and_2_out, J, NQ);
  sync_rs sync_rs_1 (.R(and_1_out), .CLK(CLK), .S(and_2_out), .RESET(RESET), .Q(sync_rs_1_q), .NQ(sync_rs_1_nq));
  not not_1 (not_1_out, CLK);
  sync_rs sync_rs_2 (.R(sync_rs_1_nq), .CLK(not_1_out), .S(sync_rs_1_q), .RESET(RESET), .Q(Q), .NQ(NQ));
endmodule

module full_adder (
  input  A,
  input  B,
  input  C_IN,
  output SUM,
  output C_OUT
);

  wire and_1_out, and_2_out, xor_1_out;

  xor xor_1 (xor_1_out, A, B);
  xor xor_2 (SUM, xor_1_out, C_IN);
  and and_1 (and_1_out, C_IN, xor_1_out);
  and and_2 (and_2_out, B, A);
  or or_1 (C_OUT, and_1_out, and_2_out);
endmodule

module adder_subtractor (
  input  [2:0] FIRST,
  input  [2:0] SECOND,
  output [2:0] RES,
  output out_4
);

  wire full_adder_1_c_out, full_adder_2_c_out, xor_1_out, xor_2_out, xor_3_out;

  xor xor_1 (xor_1_out, SECOND[0], 1'b1);
  xor xor_2 (xor_2_out, SECOND[1], 1'b1);
  xor xor_3 (xor_3_out, SECOND[2], 1'b1);
  full_adder full_adder_1 (.A(FIRST[0]), .B(xor_1_out), .C_IN(1'b1), .SUM(RES[0]), .C_OUT(full_adder_1_c_out));
  full_adder full_adder_2 (
    .A(FIRST[1]), .B(xor_2_out), .C_IN(full_adder_1_c_out), .SUM(RES[1]), .C_OUT(full_adder_2_c_out));
  full_adder full_adder_3 (.A(FIRST[2]), .B(xor_3_out), .C_IN(full_adder_2_c_out), .SUM(RES[2]), .C_OUT(out_4));
endmodule

module get_result (
  input  [3:0] ID0,
  input  [3:0] ID1,
  input  [3:0] ID2,
  input  [3:0] ID3,
  input  [3:0] ID4,
  input  [3:0] ID5,
  input  [3:0] ID6,
  input  [3:0] ID7,
  output [3:0] OUT_DATA
);

  or or_1 (OUT_DATA[0], ID0[0], ID1[0], ID2[0], ID3[0], ID4[0], ID5[0], ID6[0], ID7[0]);
  or or_2 (OUT_DATA[1], ID0[1], ID1[1], ID2[1], ID3[1], ID4[1], ID5[1], ID6[1], ID7[1]);
  or or_3 (OUT_DATA[2], ID0[2], ID1[2], ID2[2], ID3[2], ID4[2], ID5[2], ID6[2], ID7[2]);
  or or_4 (OUT_DATA[3], ID0[3], ID1[3], ID2[3], ID3[3], ID4[3], ID5[3], ID6[3], ID7[3]);
endmodule

module identification (
  input  [3:0] CUR_DATA,
  input  GET_FLAG,
  output [3:0] out_3
);

  and and_1 (out_3[0], CUR_DATA[0], GET_FLAG);
  and and_2 (out_3[1], CUR_DATA[1], GET_FLAG);
  and and_3 (out_3[2], CUR_DATA[2], GET_FLAG);
  and and_4 (out_3[3], CUR_DATA[3], GET_FLAG);
endmodule

module get_real_index (
  input  [2:0] FAKE_IDX,
  output [2:0] REAL_IDX
);

  adder_subtractor adder_subtractor_1 (.FIRST(FAKE_IDX), .SECOND(3'b001), .RES(REAL_IDX));  // open: out_4
endmodule

module conver_to_3_bit (
  input  IN_BITS,
  output [2:0] OUT_BITS
);


  assign OUT_BITS = {3{IN_BITS}};
endmodule
